# Fritzing sketch Curalink (saved by Fritzing 1.0.4)
breadboards: 1

parts:
  Mod1 = Amica NodeMCU DEVKIT 1.0
  D1 = LTE-302 [package=lte-302]
  R1 = Resistor [tolerance=±5% resistance=220 package="0805 [SMD]"]
  J1 = Basic Force Sensing Resistor (FSR) [package=THT]
  LCD2 = LCD screen
  LCM1602_IIC2 = LCM1602 IIC [part_number="LCM1602 IIC" chip_label="LCM1602 IIC" package="DIP (Dual Inline) [THT]"]
  R3 = 10K Ω Resistor [package="1206 [SMD]"]
  S1 = Pushbutton [package="[THT]"]
  U1 = RFID RC522 SIP - 8 pins [chip_label="RFID RC522" package="SIP (Single Inline) [THT]"]
  Mod2 = gy-906

nets:
  VCC: Mod1.pin1, Mod1.pin_10, Mod1.pin_26, J1.pin_1, LCM1602_IIC2.VCC, U1.VCC, Mod2.VIN
  GND: Mod1.pin2, Mod1.pin_9, Mod1.pin_25, Mod1.pin_29, D1.C, LCM1602_IIC2.GND, R3.Pin_1, S1.Pin_1, S1.Pin_2, U1.GND, Mod2.GND
  N1: Mod1.pin5, U1.NSS
  N2: Mod1.pin6, U1.MOSI
  N3: Mod1.pin7, U1.MISO
  N4: Mod1.pin8, U1.SCK
  N5: Mod1.pin_11, S1.Pin_3, S1.Pin_4
  N6: Mod1.pin_12, U1.RST
  N7: Mod1.pin_13, LCM1602_IIC2.SDA, Mod2.SDA
  N8: Mod1.pin_14, LCM1602_IIC2.SCL, Mod2.SCL
  N9: Mod1.pin_15, R1.Pin_1
  N10: Mod1.pin_16, J1.pin_0, R3.Pin_0
  N11: D1.A, R1.Pin_0
  VSS: LCD2.VSS, LCM1602_IIC2.VSS
  VDD: LCD2.VDD, LCM1602_IIC2.VDD
  N12: LCD2.V0, LCM1602_IIC2.V0
  N13: LCD2.RS, LCM1602_IIC2.RS
  N14: LCD2.R/W, LCM1602_IIC2.RW
  N15: LCD2.E, LCM1602_IIC2.E
  N16: LCD2.DB0, LCM1602_IIC2.D0
  N17: LCD2.DB1, LCM1602_IIC2.D1
  N18: LCD2.DB2, LCM1602_IIC2.D2
  N19: LCD2.DB3, LCM1602_IIC2.D3
  N20: LCD2.DB4, LCM1602_IIC2.D4
  N21: LCD2.DB5, LCM1602_IIC2.D5
  N22: LCD2.DB6, LCM1602_IIC2.D6
  N23: LCD2.DB7, LCM1602_IIC2.D7
  N24: LCD2.LED+, LCM1602_IIC2.A
  N25: LCD2.LED-, LCM1602_IIC2.K
  N26: LCM1602_IIC2.LED_A, LCM1602_IIC2.LED_B

custom parts:
  LCM1602 IIC: I2C-Module to use a 1602 or 2004 LCD on with the wire.h libory Serial LCD Modul
  10K Ω Resistor: A generic resistor
  RFID RC522 SIP - 8 pins: A SIP stand-in part for RFID RC522 . With 8 pins on a 300 mil single inline package (SIP) footprint.
  gy-906: gy-906 Non-contact PIR I2C interface temperature sensor breakout board.
